# Fritzing sketch wemos-d1-mini (saved by Fritzing 0.9.9b)
breadboards: 1

parts:
  WeMos_D1_Mini1 = WeMos-D1-mini-male-headers-below
  LCD1 = LCD screen
  RE1 = KY-040-AZ
  LCM1602_IIC1 = IC, DIP package, 22 pins [part_number="LCM1602 IIC" chip_label="LCM1602 IIC"]

nets:
  N1: WeMos_D1_Mini1.3v3, RE1.connector1, LCM1602_IIC1.pin18
  N2: WeMos_D1_Mini1.d1, LCM1602_IIC1.pin20
  N3: WeMos_D1_Mini1.d2, LCM1602_IIC1.pin19
  N4: WeMos_D1_Mini1.d5, RE1.connector4
  N5: WeMos_D1_Mini1.d6, RE1.connector3
  N6: WeMos_D1_Mini1.d7, RE1.connector2
  N7: WeMos_D1_Mini1.g, RE1.connector0, LCM1602_IIC1.pin17
  N8: LCD1.VSS, LCM1602_IIC1.pin1
  N9: LCD1.VDD, LCM1602_IIC1.pin2
  N10: LCD1.V0, LCM1602_IIC1.pin3
  N11: LCD1.RS, LCM1602_IIC1.pin4
  N12: LCD1.R/W, LCM1602_IIC1.pin5
  N13: LCD1.E, LCM1602_IIC1.pin6
  N14: LCD1.DB0, LCM1602_IIC1.pin7
  N15: LCD1.DB1, LCM1602_IIC1.pin8
  N16: LCD1.DB2, LCM1602_IIC1.pin9
  N17: LCD1.DB3, LCM1602_IIC1.pin10
  N18: LCD1.DB4, LCM1602_IIC1.pin11
  N19: LCD1.DB5, LCM1602_IIC1.pin12
  N20: LCD1.DB6, LCM1602_IIC1.pin13
  N21: LCD1.DB7, LCM1602_IIC1.pin14
  N22: LCD1.LED+, LCM1602_IIC1.pin15
  N23: LCD1.LED-, LCM1602_IIC1.pin16
  N24: LCM1602_IIC1.pin21, LCM1602_IIC1.pin22
